// Digital circuit display.dig as structural Verilog
module display (
  input  clock,
  input  [1:0] enable,
  input  [15:0] Character_Data,
  output [3:0] R,
  output [3:0] G,
  output [3:0] B,
  output H_output,
  output V_output,
  output [10:0] Character_Address
);

  wire character_position_1_p3, character_position_1_p4, character_position_2_p3, character_position_2_p4,
       character_position_3_p3, character_position_3_p4, comparator_1_lt, comparator_2_eq, comparator_3_gt,
       strings_13_p16, strings_13_p17, strings_13_p18, strings_14_p16, strings_14_p17, strings_14_p18,
       strings_15_p16, strings_15_p17, strings_15_p18, sync_1_horizontal, sync_1_picture, sync_1_vertical,
       sync_2_horizontal, sync_2_picture, sync_2_vertical, sync_3_horizontal, sync_3_picture,
       sync_3_vertical, text_1_p14, text_1_p15, text_2_p14, text_2_p15, text_3_p14, text_3_p15;
  wire [3:0] text_1_p11, text_1_p12, text_1_p13, text_2_p11, text_2_p12, text_2_p13, text_3_p11, text_3_p12,
       text_3_p13;
  wire [6:0] strings_1_character_o, strings_2_character_o, strings_3_character_o, strings_4_character_o,
       strings_5_character_o, strings_6_character_o, strings_7_character_o, strings_8_character_o,
       strings_9_character_o, strings_10_character_o, strings_11_character_o, strings_12_character_o;
  wire [7:0] character_position_1_p5, character_position_1_p6, character_position_2_p5,
       character_position_2_p6, character_position_3_p5, character_position_3_p6, strings_1_cx_o,
       strings_1_cy_o, strings_2_cx_o, strings_2_cy_o, strings_3_cx_o, strings_3_cy_o, strings_4_cx_o,
       strings_4_cy_o, strings_5_cx_o, strings_5_cy_o, strings_6_cx_o, strings_6_cy_o, strings_7_cx_o,
       strings_7_cy_o, strings_8_cx_o, strings_8_cy_o, strings_9_cx_o, strings_9_cy_o, strings_10_cx_o,
       strings_10_cy_o, strings_11_cx_o, strings_11_cy_o, strings_12_cx_o, strings_12_cy_o;
  wire [10:0] text_1_p16, text_2_p16, text_3_p16;
  wire [11:0] strings_1_background_o, strings_1_foreground_o, strings_2_background_o, strings_2_foreground_o,
       strings_3_background_o, strings_3_foreground_o, strings_4_background_o, strings_4_foreground_o,
       strings_5_background_o, strings_5_foreground_o, strings_6_background_o, strings_6_foreground_o,
       strings_7_background_o, strings_7_foreground_o, strings_8_background_o, strings_8_foreground_o,
       strings_9_background_o, strings_9_foreground_o, strings_10_background_o, strings_10_foreground_o,
       strings_11_background_o, strings_11_foreground_o, strings_12_background_o, strings_12_foreground_o;
  wire [15:0] sync_1_x, sync_1_y, sync_2_x, sync_2_y, sync_3_x, sync_3_y;

  Comparator #(.Bits(2)) comparator_1 (.a(enable), .b(2'b10), .lt(comparator_1_lt));  // open: gt, eq
  Comparator #(.Bits(2)) comparator_2 (.a(enable), .b(2'b10), .eq(comparator_2_eq));  // open: gt, lt
  Comparator #(.Bits(2)) comparator_3 (.a(enable), .b(2'b10), .gt(comparator_3_gt));  // open: eq, lt
  sync sync_1 (
    .clock(clock), .resolution_x(16'h280), .front_porch_x(16'h10), .sync_x(16'h60), .back_porch_x(16'h30),
    .resolution_y(16'h1e0), .front_porch_y(16'hb), .sync_y(16'h2), .back_porch_y(16'h21), .negative(1'b1),
    .Horizontal(sync_1_horizontal), .Vertical(sync_1_vertical), .picture(sync_1_picture), .X(sync_1_x),
    .Y(sync_1_y));
  sync sync_2 (
    .clock(clock), .resolution_x(16'h320), .front_porch_x(16'h28), .sync_x(16'h80), .back_porch_x(16'h58),
    .resolution_y(16'h258), .front_porch_y(16'h2), .sync_y(16'h4), .back_porch_y(16'h17), .negative(1'b0),
    .Horizontal(sync_2_horizontal), .Vertical(sync_2_vertical), .picture(sync_2_picture), .X(sync_2_x),
    .Y(sync_2_y));
  sync sync_3 (
    .clock(clock), .resolution_x(16'h500), .front_porch_x(16'h6e), .sync_x(16'h28), .back_porch_x(16'hdc),
    .resolution_y(16'h2d0), .front_porch_y(16'h6), .sync_y(16'h5), .back_porch_y(16'h14), .negative(1'b0),
    .Horizontal(sync_3_horizontal), .Vertical(sync_3_vertical), .picture(sync_3_picture), .X(sync_3_x),
    .Y(sync_3_y));
  // character_position character_position_1: pin names not known; wires that end beside it: sync_1_x, sync_1_y, character_position_1_p3, character_position_1_p4, character_position_1_p5, character_position_1_p6
  // character_position character_position_2: pin names not known; wires that end beside it: sync_2_x, sync_2_y, character_position_2_p3, character_position_2_p4, character_position_2_p5, character_position_2_p6
  // character_position character_position_3: pin names not known; wires that end beside it: sync_3_x, sync_3_y, character_position_3_p3, character_position_3_p4, character_position_3_p5, character_position_3_p6
  strings strings_1 (
    .CX(character_position_1_p5), .CY(character_position_1_p6), .foreground(12'h9e), .background({12{1'b0}}),
    .character(7'b1000000), .foreground__colour({12{1'b1}}), .background__colour(12'hf00),
    .CX__colour(6'b000001), .CY_colour(8'h7), .Character_0(7'b0111000), .Character_1(7'b0101101),
    .Character_2(7'b1000010), .Character_3(7'b1010101), .cutoff(8'h7), .enable(comparator_1_lt),
    .CX_o(strings_1_cx_o), .CY_o(strings_1_cy_o), .foreground_o(strings_1_foreground_o),
    .background_o(strings_1_background_o), .character_o(strings_1_character_o));
  strings strings_2 (
    .CX(character_position_2_p5), .CY(character_position_2_p6), .foreground(12'h9e), .background({12{1'b0}}),
    .character(7'b1000000), .foreground__colour({12{1'b1}}), .background__colour(12'hf00),
    .CX__colour(6'b000100), .CY_colour(8'h9), .Character_0(7'b0111000), .Character_1(7'b0101101),
    .Character_2(7'b1000010), .Character_3(7'b1010101), .cutoff(8'h9), .enable(comparator_2_eq),
    .CX_o(strings_2_cx_o), .CY_o(strings_2_cy_o), .foreground_o(strings_2_foreground_o),
    .background_o(strings_2_background_o), .character_o(strings_2_character_o));
  strings strings_3 (
    .CX(character_position_3_p5), .CY(character_position_3_p6), .foreground(12'h9e), .background({12{1'b0}}),
    .character(7'b1000000), .foreground__colour({12{1'b1}}), .background__colour(12'hf00),
    .CX__colour(6'b000111), .CY_colour(8'ha), .Character_0(7'b0111000), .Character_1(7'b0101101),
    .Character_2(7'b1000010), .Character_3(7'b1010101), .cutoff(8'ha), .enable(comparator_3_gt),
    .CX_o(strings_3_cx_o), .CY_o(strings_3_cy_o), .foreground_o(strings_3_foreground_o),
    .background_o(strings_3_background_o), .character_o(strings_3_character_o));
  strings strings_4 (
    .CX(strings_1_cx_o), .CY(strings_1_cy_o), .foreground(strings_1_foreground_o),
    .background(strings_1_background_o), .character(strings_1_character_o), .foreground__colour({12{1'b0}}),
    .background__colour(12'h6f2), .CX__colour(6'b000010), .CY_colour(8'h7), .Character_0(7'b1010100),
    .Character_1(7'b0100000), .Character_2(7'b1001101), .Character_3(7'b1001001), .cutoff(8'h7),
    .enable(comparator_1_lt), .CX_o(strings_4_cx_o), .CY_o(strings_4_cy_o),
    .foreground_o(strings_4_foreground_o), .background_o(strings_4_background_o),
    .character_o(strings_4_character_o));
  strings strings_5 (
    .CX(strings_2_cx_o), .CY(strings_2_cy_o), .foreground(strings_2_foreground_o),
    .background(strings_2_background_o), .character(strings_2_character_o), .foreground__colour({12{1'b0}}),
    .background__colour(12'h6f2), .CX__colour(6'b000101), .CY_colour(8'h9), .Character_0(7'b1010100),
    .Character_1(7'b0100000), .Character_2(7'b1001101), .Character_3(7'b1001001), .cutoff(8'h9),
    .enable(comparator_2_eq), .CX_o(strings_5_cx_o), .CY_o(strings_5_cy_o),
    .foreground_o(strings_5_foreground_o), .background_o(strings_5_background_o),
    .character_o(strings_5_character_o));
  strings strings_6 (
    .CX(strings_3_cx_o), .CY(strings_3_cy_o), .foreground(strings_3_foreground_o),
    .background(strings_3_background_o), .character(strings_3_character_o), .foreground__colour({12{1'b0}}),
    .background__colour(12'h6f2), .CX__colour(6'b001000), .CY_colour(8'ha), .Character_0(7'b1010100),
    .Character_1(7'b0100000), .Character_2(7'b1001101), .Character_3(7'b1001001), .cutoff(8'ha),
    .enable(comparator_3_gt), .CX_o(strings_6_cx_o), .CY_o(strings_6_cy_o),
    .foreground_o(strings_6_foreground_o), .background_o(strings_6_background_o),
    .character_o(strings_6_character_o));
  strings strings_7 (
    .CX(strings_4_cx_o), .CY(strings_4_cy_o), .foreground(strings_4_foreground_o),
    .background(strings_4_background_o), .character(strings_4_character_o), .foreground__colour(12'hf17),
    .background__colour(12'hff), .CX__colour(6'b000011), .CY_colour(8'h7), .Character_0(7'b1000111),
    .Character_1(7'b1001000), .Character_2(7'b1010100), .Character_3(7'b1011001), .cutoff(8'h7),
    .enable(comparator_1_lt), .CX_o(strings_7_cx_o), .CY_o(strings_7_cy_o),
    .foreground_o(strings_7_foreground_o), .background_o(strings_7_background_o),
    .character_o(strings_7_character_o));
  strings strings_8 (
    .CX(strings_5_cx_o), .CY(strings_5_cy_o), .foreground(strings_5_foreground_o),
    .background(strings_5_background_o), .character(strings_5_character_o), .foreground__colour(12'hf17),
    .background__colour(12'hff), .CX__colour(6'b000110), .CY_colour(8'h9), .Character_0(7'b1000111),
    .Character_1(7'b1001000), .Character_2(7'b1010100), .Character_3(7'b1011001), .cutoff(8'h9),
    .enable(comparator_2_eq), .CX_o(strings_8_cx_o), .CY_o(strings_8_cy_o),
    .foreground_o(strings_8_foreground_o), .background_o(strings_8_background_o),
    .character_o(strings_8_character_o));
  strings strings_9 (
    .CX(strings_6_cx_o), .CY(strings_6_cy_o), .foreground(strings_6_foreground_o),
    .background(strings_6_background_o), .character(strings_6_character_o), .foreground__colour(12'hf17),
    .background__colour(12'hff), .CX__colour(6'b001001), .CY_colour(8'ha), .Character_0(7'b1000111),
    .Character_1(7'b1001000), .Character_2(7'b1010100), .Character_3(7'b1011001), .cutoff(8'ha),
    .enable(comparator_3_gt), .CX_o(strings_9_cx_o), .CY_o(strings_9_cy_o),
    .foreground_o(strings_9_foreground_o), .background_o(strings_9_background_o),
    .character_o(strings_9_character_o));
  strings strings_10 (
    .CX(strings_7_cx_o), .CY(strings_7_cy_o), .foreground(strings_7_foreground_o),
    .background(strings_7_background_o), .character(strings_7_character_o), .foreground__colour(12'h451),
    .background__colour(12'heff), .CX__colour(6'b000100), .CY_colour(8'h7), .Character_0(7'b0100000),
    .Character_1(7'b1010110), .Character_2(7'b1000111), .Character_3(7'b1000001), .cutoff(8'h7),
    .enable(comparator_1_lt), .CX_o(strings_10_cx_o), .CY_o(strings_10_cy_o),
    .foreground_o(strings_10_foreground_o), .background_o(strings_10_background_o),
    .character_o(strings_10_character_o));
  strings strings_11 (
    .CX(strings_8_cx_o), .CY(strings_8_cy_o), .foreground(strings_8_foreground_o),
    .background(strings_8_background_o), .character(strings_8_character_o), .foreground__colour(12'h451),
    .background__colour(12'heff), .CX__colour(6'b000111), .CY_colour(8'h9), .Character_0(7'b0100000),
    .Character_1(7'b1010110), .Character_2(7'b1000111), .Character_3(7'b1000001), .cutoff(8'h9),
    .enable(comparator_2_eq), .CX_o(strings_11_cx_o), .CY_o(strings_11_cy_o),
    .foreground_o(strings_11_foreground_o), .background_o(strings_11_background_o),
    .character_o(strings_11_character_o));
  strings strings_12 (
    .CX(strings_9_cx_o), .CY(strings_9_cy_o), .foreground(strings_9_foreground_o),
    .background(strings_9_background_o), .character(strings_9_character_o), .foreground__colour(12'h451),
    .background__colour(12'heff), .CX__colour(6'b001010), .CY_colour(8'ha), .Character_0(7'b0100000),
    .Character_1(7'b1010110), .Character_2(7'b1000111), .Character_3(7'b1000001), .cutoff(8'ha),
    .enable(comparator_3_gt), .CX_o(strings_12_cx_o), .CY_o(strings_12_cy_o),
    .foreground_o(strings_12_foreground_o), .background_o(strings_12_background_o),
    .character_o(strings_12_character_o));
  // strings strings_13: pin names not known; wires that end beside it: strings_10_cx_o, strings_10_cy_o, strings_10_foreground_o, strings_10_background_o, strings_10_character_o, 12'h342, 12'he9, 6'b000101, 8'h7, 7'b0100000, 7'b0110100, 7'b0111000, 7'b0110000, 8'h7, comparator_1_lt, strings_13_p16, strings_13_p17, strings_13_p18
  // strings strings_14: pin names not known; wires that end beside it: strings_11_cx_o, strings_11_cy_o, strings_11_foreground_o, strings_11_background_o, strings_11_character_o, 12'h342, 12'he9, 6'b001000, 8'h9, 7'b0100000, 7'b0110110, 7'b0110000, 7'b0110000, 8'h9, comparator_2_eq, strings_14_p16, strings_14_p17, strings_14_p18
  // strings strings_15: pin names not known; wires that end beside it: strings_12_cx_o, strings_12_cy_o, strings_12_foreground_o, strings_12_background_o, strings_12_character_o, 12'h342, 12'he9, 6'b001011, 8'ha, 7'b0100000, 7'b0110111, 7'b0110010, 7'b0110000, 8'ha, comparator_3_gt, strings_15_p16, strings_15_p17, strings_15_p18
  // text text_1: pin names not known; wires that end beside it: sync_1_horizontal, sync_1_vertical, sync_1_picture, character_position_1_p3, character_position_1_p4, clock, strings_13_p16, strings_13_p17, strings_13_p18, Character_Data, text_1_p11, text_1_p12, text_1_p13, text_1_p14, text_1_p15, text_1_p16
  // text text_2: pin names not known; wires that end beside it: sync_2_horizontal, sync_2_vertical, sync_2_picture, character_position_2_p3, character_position_2_p4, clock, strings_14_p16, strings_14_p17, strings_14_p18, Character_Data, text_2_p11, text_2_p12, text_2_p13, text_2_p14, text_2_p15, text_2_p16
  // text text_3: pin names not known; wires that end beside it: sync_3_horizontal, sync_3_vertical, sync_3_picture, character_position_3_p3, character_position_3_p4, clock, strings_15_p16, strings_15_p17, strings_15_p18, Character_Data, text_3_p11, text_3_p12, text_3_p13, text_3_p14, text_3_p15, text_3_p16
  Multiplexer #(.Selector_Bits(2), .Bits(4)) multiplexer_1 (
    .sel(enable), .in_0(4'b0000), .in_1(text_1_p11), .in_2(text_2_p11), .in_3(text_3_p11), .out(R));
  Multiplexer #(.Selector_Bits(2), .Bits(4)) multiplexer_2 (
    .sel(enable), .in_0(4'b0000), .in_1(text_1_p12), .in_2(text_2_p12), .in_3(text_3_p12), .out(G));
  Multiplexer #(.Selector_Bits(2), .Bits(4)) multiplexer_3 (
    .sel(enable), .in_0(4'b0000), .in_1(text_1_p13), .in_2(text_2_p13), .in_3(text_3_p13), .out(B));
  Multiplexer #(.Selector_Bits(2)) multiplexer_4 (
    .sel(enable), .in_0(1'b0), .in_1(text_1_p14), .in_2(text_2_p14), .in_3(text_3_p14), .out(H_output));
  Multiplexer #(.Selector_Bits(2)) multiplexer_5 (
    .sel(enable), .in_0(1'b0), .in_1(text_1_p15), .in_2(text_2_p15), .in_3(text_3_p15), .out(V_output));
  Multiplexer #(.Selector_Bits(2), .Bits(11)) multiplexer_6 (
    .sel(enable), .in_0({11{1'b0}}), .in_1(text_1_p16), .in_2(text_2_p16), .in_3(text_3_p16),
    .out(Character_Address));

  // Other names for the same wires on the sheet: C = clock

  // Notes on the sheet:
  //   clock: Hz: 2147483647
endmodule
