// Digital circuit strings.dig as structural Verilog
module strings (
  input  [7:0] CX,
  input  [7:0] CY,
  input  [11:0] foreground,
  input  [11:0] background,
  input  [6:0] character,
  input  [11:0] foreground__colour,
  input  [11:0] background__colour,
  input  [3:0] CX__colour,
  input  [7:0] CY_colour,
  input  [6:0] Character_0,
  input  [6:0] Character_1,
  input  [6:0] Character_2,
  input  [6:0] Character_3,
  input  [6:0] Character_4,
  input  [6:0] Character_5,
  input  [6:0] Character_6,
  input  [6:0] Character_7,
  input  [6:0] Character_8,
  input  [6:0] Character_9,
  input  [6:0] Character_10,
  input  [6:0] Character_11,
  input  [6:0] Character_12,
  input  [6:0] Character_13,
  input  [6:0] Character_14,
  input  [6:0] Character_15,
  input  enable,
  output [6:0] character_o,
  output [11:0] foreground_o,
  output [11:0] background_o,
  output [7:0] CX_o,
  output [7:0] CY_o
);

  wire and_1_out, comparator_1_eq, comparator_2_gt;
  wire [6:0] multiplexer_1_out;

  Multiplexer #(.Selector_Bits(4), .Bits(7)) multiplexer_1 (
    .sel(CX[3:0]), .in_0(Character_0), .in_1(Character_1), .in_2(Character_2), .in_3(Character_3),
    .in_4(Character_4), .in_5(Character_5), .in_6(Character_6), .in_7(Character_7), .in_8(Character_8),
    .in_9(Character_9), .in_10(Character_10), .in_11(Character_11), .in_12(Character_12),
    .in_13(Character_13), .in_14(Character_14), .in_15(Character_15), .out(multiplexer_1_out));
  Comparator #(.Bits(4)) comparator_1 (.a(CX[7:4]), .b(CX__colour), .eq(comparator_1_eq));  // open: gt, lt
  Comparator #(.Bits(8)) comparator_2 (.a(CY), .b(CY_colour), .gt(comparator_2_gt));  // open: eq, lt
  and and_1 (and_1_out, comparator_1_eq, enable, comparator_2_gt);
  Multiplexer #(.Bits(7)) multiplexer_2 (
    .sel(and_1_out), .in_0(character), .in_1(multiplexer_1_out), .out(character_o));
  Multiplexer #(.Bits(12)) multiplexer_3 (
    .sel(and_1_out), .in_0(foreground), .in_1(foreground__colour), .out(foreground_o));
  Multiplexer #(.Bits(12)) multiplexer_4 (
    .sel(and_1_out), .in_0(background), .in_1(background__colour), .out(background_o));

  assign CX_o = CX;
  assign CY_o = CY;
endmodule
