// Digital circuit sync.dig as structural Verilog
module sync (
  input  clock,
  input  [15:0] resolution_x,
  input  [15:0] front_porch_x,
  input  [15:0] sync_x,
  input  [15:0] back_porch_x,
  input  [15:0] resolution_y,
  input  [15:0] front_porch_y,
  input  [15:0] sync_y,
  input  [15:0] back_porch_y,
  input  negative,
  output Horizontal,
  output Vertical,
  output picture,
  output [15:0] X,
  output [15:0] Y
);

  wire comparator_1_lt, comparator_2_lt, timing_1_next;

  timing timing_1 (
    .enable(1'b1), .clock(clock), .resolution(resolution_x), .front_porch(front_porch_x), .sync(sync_x),
    .back_porch(back_porch_x), .negative(negative), .V(X), .pulse(Horizontal), .next(timing_1_next));
  timing timing_2 (
    .enable(timing_1_next), .clock(clock), .resolution(resolution_y), .front_porch(front_porch_y),
    .sync(sync_y), .back_porch(back_porch_y), .negative(negative), .V(Y), .pulse(Vertical));  // open: next
  Comparator #(.Bits(16)) comparator_1 (.a(X), .b(resolution_x), .lt(comparator_1_lt));  // open: gt, eq
  Comparator #(.Bits(16)) comparator_2 (.a(Y), .b(resolution_y), .lt(comparator_2_lt));  // open: gt, eq
  and and_1 (picture, comparator_1_lt, comparator_2_lt);

  // Other names for the same wires on the sheet: C = clock

  // Notes on the sheet:
  //   clock: Hz: 2147483647
endmodule
