// Digital circuit vga_sync.dig as structural Verilog
module vga_sync (
  input  clock,
  output Horizontal,
  output Vertical,
  output picture,
  output [15:0] X,
  output [15:0] Y
);

  wire comparator_1_lt, comparator_2_lt, Horizontal_next;

  vga_timing u_Horizontal (
    .enable(1'b1), .clock(clock), .resolution(16'h500), .front_porch(16'h6e), .sync(16'h28),
    .back_porch(16'hdc), .negative(1'b0), .V(X), .pulse(Horizontal), .next(Horizontal_next));
  vga_timing u_Vertical (
    .enable(Horizontal_next), .clock(clock), .resolution(16'h2d0), .front_porch(16'h5), .sync(16'h5),
    .back_porch(16'h15), .negative(1'b0), .V(Y), .pulse(Vertical));  // open: next
  Comparator #(.Bits(16)) comparator_1 (.a(X), .b(16'h500), .lt(comparator_1_lt));  // open: gt, eq
  Comparator #(.Bits(16)) comparator_2 (.a(Y), .b(16'h2d0), .lt(comparator_2_lt));  // open: gt, eq
  and and_1 (picture, comparator_1_lt, comparator_2_lt);

  // Other names for the same wires on the sheet: C = clock

  // Notes on the sheet:
  //   clock: Hz: 2147483647
endmodule
