// Digital circuit vga_text.dig as structural Verilog
module vga_text (
  input  H_input,
  input  V_input,
  input  picture,
  input  [4:0] row,
  input  [3:0] column,
  input  clock,
  input  [6:0] character,
  input  [11:0] foreground,
  input  [11:0] background,
  input  [15:0] Character_Data,
  output [3:0] R,
  output [3:0] G,
  output [3:0] B,
  output H_output,
  output V_output,
  output [10:0] Character_Address
);

  wire sub_1_c_o;
  wire [1:0] d_ff_4_q;
  wire [3:0] d_ff_3_q;
  wire [6:0] sub_1_s;
  wire [11:0] d_ff_5_q, d_ff_6_q;

  Sub #(.Bits(7)) sub_1 (.a(character), .b(7'b0100000), .c_i(1'b0), .s(sub_1_s), .c_o(sub_1_c_o));
  D_FF d_ff_1 (.D(H_input), .C(clock), .Q(H_output));  // open: nQ
  D_FF d_ff_2 (.D(V_input), .C(clock), .Q(V_output));  // open: nQ
  D_FF #(.Bits(4)) d_ff_3 (.D(column), .C(clock), .Q(d_ff_3_q));  // open: nQ
  Multiplexer #(.Bits(6)) multiplexer_1 (
    .sel(sub_1_c_o), .in_0(sub_1_s[5:0]), .in_1({6{1'b0}}), .out(Character_Address[10:5]));
  D_FF d_ff_4 (.D(picture), .C(clock), .Q(d_ff_4_q[1]));  // open: nQ
  D_FF #(.Bits(12)) d_ff_5 (.D(background), .C(clock), .Q(d_ff_5_q));  // open: nQ
  D_FF #(.Bits(12)) d_ff_6 (.D(foreground), .C(clock), .Q(d_ff_6_q));  // open: nQ
  Multiplexer #(.Selector_Bits(4)) multiplexer_2 (
    .sel(d_ff_3_q), .in_0(Character_Data[15]), .in_1(Character_Data[14]), .in_2(Character_Data[13]),
    .in_3(Character_Data[12]), .in_4(Character_Data[11]), .in_5(Character_Data[10]),
    .in_6(Character_Data[9]), .in_7(Character_Data[8]), .in_8(Character_Data[7]), .in_9(Character_Data[6]),
    .in_10(Character_Data[5]), .in_11(Character_Data[4]), .in_12(Character_Data[3]),
    .in_13(Character_Data[2]), .in_14(Character_Data[1]), .in_15(Character_Data[0]), .out(d_ff_4_q[0]));
  Multiplexer #(.Selector_Bits(2), .Bits(12)) multiplexer_3 (
    .sel(d_ff_4_q), .in_0({12{1'b0}}), .in_1({12{1'b0}}), .in_2(d_ff_5_q), .in_3(d_ff_6_q), .out({R, G, B}));

  assign Character_Address[4:0] = row;

  // Other names for the same wires on the sheet: C = clock

  // Notes on the sheet:
  //   clock: Hz: 2147483647
endmodule
